# Fritzing sketch sensor (saved by Fritzing 0.9.3b)

parts:
  MCU1 = Raspberry Pi Zero
  SONAR1 = Maxbotix MaxSonar Ultrasonic Sensor
  Part1 = Adafruit Micro USB Breakout [part_number="Adafruit #1833"]
  ENC28J1 = ENC28J60

nets:
  N1: MCU1.pin_1, MCU1.pin_17, ENC28J1.3.3
  N2: MCU1.pin_2, MCU1.pin_4, SONAR1.+5V, Part1.VBUS
  GND: MCU1.pin_6, MCU1.pin_9, MCU1.pin_39, SONAR1.GND, Part1.GND, ENC28J1.GND
  N3: MCU1.pin_10, SONAR1.TX
  N4: MCU1.pin_15, SONAR1.RX
  N5: MCU1.pin_19, ENC28J1.SI
  N6: MCU1.pin_21, MCU1.pin_22, ENC28J1.INT, ENC28J1.SO
  N7: MCU1.pin_23, ENC28J1.SCK
  N8: MCU1.pin_24, ENC28J1.CS

custom parts:
  Maxbotix MaxSonar Ultrasonic Sensor: Maxbotix MaxSonar Ultrasonic Sensor LV-EZ0, LV-EZ1, LV-EZ2, LV-EZ3, LV-EZ4
  Adafruit Micro USB Breakout: Simple but effective - this breakout board has a USB Micro-B connector, with all 5 pins broken out. Great for pairing with a microcontroller with USB support, or adding USB 5V power to a project. We use a micro-AB connector with through-hole shielding pads for an excellent strong connection - it won't rip off by accident! Comes with one fully assembled and tested micro B breakout PCB and a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
  ENC28J60: Ethernet Module ENC28J60
